// Logisim project Logic Gates.circ as structural Verilog: 1 circuit, main circuit main
module main (
  input  in_1,
  input  in_2,
  input  in_3,
  input  in_4,
  input  in_5,
  input  in_6,
  input  in_7,
  input  in_8,
  input  in_9,
  input  in_10,
  input  in_11,
  input  in_12,
  input  in_13,
  input  in_14,
  input  in_15,
  input  in_16,
  input  in_17,
  input  in_18,
  input  in_19,
  input  in_20,
  input  in_21,
  output out_22,
  output out_23,
  output out_24,
  output out_25,
  output out_26,
  output out_27,
  output out_28,
  output out_29,
  output out_30
);

  wire and_1_out, and_2_out, and_3_out, and_4_out, and_5_out, and_6_out, and_7_out, and_8_out, not_1_out,
       not_2_out, not_3_out, not_4_out, not_5_out, not_6_out, or_1_out, or_2_out, or_4_out, or_5_out,
       or_6_out;

  not not_1 (not_1_out, in_4);
  not not_2 (not_2_out, in_5);
  or or_1 (or_1_out, in_9, in_10);
  and and_1 (and_1_out, in_11, in_12);
  not not_3 (not_3_out, in_14);
  not not_4 (not_4_out, in_15);
  not not_5 (not_5_out, in_17);
  or or_2 (or_2_out, in_18, in_19);
  not not_6 (not_6_out, in_20);
  and and_2 (and_2_out, in_4, in_5);
  and and_3 (and_3_out, not_1_out, not_2_out);
  and and_4 (and_4_out, in_6, in_8);
  and and_5 (and_5_out, in_6, in_7);
  not not_7 (out_25, or_1_out);
  LED led_1 (.in(out_25));
  or or_3 (out_26, and_1_out, in_13);
  LED led_2 (.in(out_26));
  and and_6 (and_6_out, in_14, in_15);
  or or_4 (or_4_out, not_3_out, not_4_out);
  and and_7 (and_7_out, in_16, in_17);
  and and_8 (and_8_out, in_16, not_5_out);
  and and_9 (out_29, or_2_out, in_19);
  or or_5 (or_5_out, not_6_out, in_21);
  xor xor_1 (out_22, in_2, in_3);
  or or_6 (or_6_out, and_2_out, and_3_out);
  or or_7 (out_24, and_4_out, and_5_out);
  or or_8 (out_27, and_6_out, or_4_out);
  LED led_3 (.in(out_27));
  or or_9 (out_28, and_7_out, and_8_out);
  LED led_4 (.in(out_28));
  LED led_5 (.in(out_29));
  and and_10 (out_30, in_20, or_5_out);
  LED led_6 (.in(out_30));
  LED led_7 (.in(out_22));
  not not_8 (out_23, or_6_out);
  LED led_8 (.in(out_24));
  LED led_9 (.in(out_23));

  // Notes on the sheet:
  //   6(a)
  //   6(b)
  //   7(a).
  //   7(b)
  //   7(c)
endmodule
